# Fritzing sketch wiring (saved by Fritzing 0.9.3b)
breadboards: 1

parts:
  R1 = Resistor [tolerance=±5% resistance=330 package=THT]
  R2 = Resistor [tolerance=±5% resistance=470 package=THT]
  Raspberry_Pi_1 = Raspberry Pi 3 [part_number=RPI-3-V1.2]
  HC-SR04_Sensor_1 = HC-SR04 Ultrasonic Distance Sensor
  S1 = Pushbutton [package="[THT]"]
  Součástka1 = SSOP24 [chip_label=Thermometer package=SSOP]
  R3 = Resistor [tolerance=±5% resistance=220 package=THT]
  U1 = Sharp PC817 [package=THT]

nets:
  N1: R1.Pin_0, HC-SR04_Sensor_1.ECHO
  3V3: R1.Pin_1, R2.Pin_0, Raspberry_Pi_1.3v3, Raspberry_Pi_1.GPIO2, Raspberry_Pi_1.GPIO27, Raspberry_Pi_1.3V3, Raspberry_Pi_1.GPIO24, Raspberry_Pi_1.GPIO23, Raspberry_Pi_1.5V, HC-SR04_Sensor_1.VCC, Součástka1.3
  GND: R2.Pin_1, Raspberry_Pi_1.GPIO11, Raspberry_Pi_1.GND, Raspberry_Pi_1.ID_SD, Raspberry_Pi_1.GPIO7, Raspberry_Pi_1.GPIO18, Raspberry_Pi_1.GPIO14, HC-SR04_Sensor_1.TRIG, HC-SR04_Sensor_1.GND, Součástka1.4, U1.Pin_2
  N2: Raspberry_Pi_1.GPIO8, Raspberry_Pi_1.GPIO25, R3.Pin_0
  N3: Raspberry_Pi_1.GPIO15, Součástka1.1
  N4: S1.Pin_1, S1.Pin_2, U1.Pin_3
  N5: S1.Pin_3, S1.Pin_4, U1.Pin_4

notes:
  For UART connection use jumper JP15 (TX) -> RPi RX
  For power source use + and - (instead of batteries)
  For button - connect U pin 3 to button K1's GND pin on board
